// Logisim project mainProjw7Seg (2).circ as structural Verilog: 10 circuits, main circuit main
module main (
  input  E,
  input  X,
  input  R
);

  wire CLK_out, sseg_1_p2, sseg_1_p3, sseg_1_p4, sseg_1_p5, sseg_1_p6, sseg_1_p7, sseg_1_p8,
       trafficcontroller_1_le_0, trafficcontroller_1_le_1, trafficcontroller_1_lx_0,
       trafficcontroller_1_lx_1, trafficlight_1_green, trafficlight_1_red, trafficlight_1_yellow,
       trafficlight_2_green, trafficlight_2_red, trafficlight_2_yellow;
  wire [3:0] trafficcontroller_1_c_3;

  Clock #(.highDuration(5), .lowDuration(5)) CLK (.out(CLK_out));
  TrafficController trafficcontroller_1 (
    .C_1(trafficcontroller_1_c_3[2]), .C0(trafficcontroller_1_c_3[3]), .C_2(trafficcontroller_1_c_3[1]),
    .C_3(trafficcontroller_1_c_3[0]), .LE_1(trafficcontroller_1_le_1), .LE_0(trafficcontroller_1_le_0),
    .LX_1(trafficcontroller_1_lx_1), .LX_0(trafficcontroller_1_lx_0), .E(E), .X(X), .CLK(CLK_out), .R(R));
  TrafficLight trafficlight_1 (
    .Red(trafficlight_1_red), .Yellow(trafficlight_1_yellow), .Green(trafficlight_1_green),
    .L_0(trafficcontroller_1_le_0), .L_1(trafficcontroller_1_le_1));
  TrafficLight trafficlight_2 (
    .Red(trafficlight_2_red), .Yellow(trafficlight_2_yellow), .Green(trafficlight_2_green),
    .L_0(trafficcontroller_1_lx_0), .L_1(trafficcontroller_1_lx_1));
  // SSeg sseg_1: pin names not known; wires that end beside it: trafficcontroller_1_c_3, sseg_1_p2, sseg_1_p3, sseg_1_p4, sseg_1_p5, sseg_1_p6, sseg_1_p7, sseg_1_p8
  LED led_1 (.in(trafficlight_1_red));
  LED led_2 (.in(trafficlight_1_yellow));
  LED led_3 (.in(trafficlight_1_green));
  LED led_4 (.in(trafficlight_2_red));
  LED led_5 (.in(trafficlight_2_yellow));
  LED led_6 (.in(trafficlight_2_green));
  _7_Segment_Display u_7_segment_display_1 (
    .g(sseg_1_p8), .f(sseg_1_p7), .a(sseg_1_p2), .b(sseg_1_p3), .e(sseg_1_p6), .d(sseg_1_p5), .c(sseg_1_p4));  // open: dp

  // Notes on the sheet:
  //   Entrance 
  //   Exit
endmodule

module SRLatch (
  input  R,
  input  S,
  output Q,
  output out_4
);

  nor nor_1 (Q, R, out_4);
  nor nor_2 (out_4, Q, S);
endmodule

module DLatch (
  input  CLK,
  input  D,
  output Q,
  output out_4
);

  wire and_1_out, and_2_out, not_1_out;

  not not_1 (not_1_out, D);
  and and_1 (and_1_out, CLK, not_1_out);
  and and_2 (and_2_out, CLK, D);
  SRLatch srlatch_1 (.Q(Q), .out_4(out_4), .R(and_1_out), .S(and_2_out));
endmodule

module flipflop (
  input  CLK,
  input  D,
  output Q,
  output out_4
);

  wire dlatch_1_q, not_1_out;

  not not_1 (not_1_out, CLK);
  DLatch dlatch_1 (.Q(dlatch_1_q), .CLK(not_1_out), .D(D));  // open: out_4
  DLatch dlatch_2 (.Q(Q), .out_4(out_4), .CLK(CLK), .D(dlatch_1_q));
endmodule

module StateRegister (
  input  CLK,
  input  D_1,
  input  D_2,
  input  D_3,
  input  D_4,
  input  D_5,
  input  D_6,
  input  R,
  output Q_1,
  output Q_2,
  output Q_3,
  output Q_4,
  output Q_5,
  output Q_6
);

  wire and_1_out, and_2_out, and_3_out, and_4_out, and_5_out, and_6_out, not_1_out;

  not not_1 (not_1_out, R);
  and and_1 (and_1_out, D_1, not_1_out);
  and and_2 (and_2_out, D_2, not_1_out);
  and and_3 (and_3_out, D_3, not_1_out);
  and and_4 (and_4_out, D_4, not_1_out);
  and and_5 (and_5_out, D_5, not_1_out);
  and and_6 (and_6_out, D_6, not_1_out);
  flipflop flipflop_1 (.Q(Q_1), .D(and_1_out), .CLK(CLK));  // open: out_4
  flipflop flipflop_2 (.Q(Q_2), .D(and_2_out), .CLK(CLK));  // open: out_4
  flipflop flipflop_3 (.Q(Q_3), .D(and_3_out), .CLK(CLK));  // open: out_4
  flipflop flipflop_4 (.Q(Q_4), .D(and_4_out), .CLK(CLK));  // open: out_4
  flipflop flipflop_5 (.Q(Q_5), .D(and_5_out), .CLK(CLK));  // open: out_4
  flipflop flipflop_6 (.Q(Q_6), .D(and_6_out), .CLK(CLK));  // open: out_4
endmodule

module TrafficController (
  input  E,
  input  X,
  input  CLK,
  input  R,
  output LE_1,
  output LE_0,
  output LX_1,
  output LX_0,
  output C0,
  output C_1,
  output C_2,
  output C_3
);

  wire and_1_out, and_2_out, and_3_out, and_4_out, and_5_out, and_6_out, and_7_out, and_8_out, and_9_out,
       and_10_out, and_11_out, and_12_out, and_13_out, and_14_out, and_15_out, and_16_out, and_17_out,
       and_18_out, and_19_out, and_20_out, and_21_out, and_22_out, and_23_out, and_24_out, and_25_out,
       and_26_out, and_27_out, and_28_out, and_29_out, and_30_out, and_31_out, and_32_out, and_33_out,
       and_34_out, and_35_out, and_36_out, and_37_out, and_38_out, and_39_out, and_40_out, and_41_out,
       and_42_out, and_43_out, and_44_out, and_45_out, and_46_out, and_47_out, and_48_out, and_49_out,
       and_50_out, and_51_out, and_52_out, and_53_out, and_54_out, and_55_out, and_56_out, and_57_out,
       and_58_out, and_59_out, and_60_out, and_61_out, and_62_out, and_63_out, and_64_out, and_65_out,
       and_66_out, and_67_out, and_68_out, and_69_out, and_70_out, and_71_out, and_72_out, and_73_out,
       and_74_out, and_75_out, and_76_out, and_77_out, and_78_out, and_79_out, and_80_out, and_81_out,
       and_82_out, and_83_out, and_84_out, and_85_out, and_86_out, and_87_out, and_88_out, and_89_out,
       and_90_out, and_91_out, and_92_out, and_93_out, and_94_out, and_95_out, and_96_out, and_97_out,
       and_98_out, and_99_out, and_100_out, and_101_out, and_102_out, and_103_out, and_104_out, and_105_out,
       and_106_out, and_107_out, and_108_out, and_109_out, and_110_out, and_111_out, and_112_out,
       and_113_out, and_114_out, and_115_out, and_116_out, and_117_out, and_118_out, and_119_out, or_1_out,
       or_2_out, or_3_out, or_4_out, or_5_out, or_6_out, stateregister_1_q_1, stateregister_1_q_2,
       stateregister_1_q_3, stateregister_1_q_4, stateregister_1_q_5, stateregister_1_q_6;

  and and_1 (and_1_out, E, ~stateregister_1_q_1, ~stateregister_1_q_4, ~stateregister_1_q_5, ~stateregister_1_q_6);  // AND_Gate
  and and_2 (and_2_out, ~X, E, ~stateregister_1_q_1, ~stateregister_1_q_2, ~stateregister_1_q_6);  // AND_Gate
  and and_3 (and_3_out, ~X, E, ~stateregister_1_q_1, ~stateregister_1_q_2, ~stateregister_1_q_4);  // AND_Gate
  and and_4 (and_4_out, ~X, E, ~stateregister_1_q_1, ~stateregister_1_q_2, ~stateregister_1_q_3);  // AND_Gate
  and and_5 (and_5_out, ~E, stateregister_1_q_1, ~stateregister_1_q_4, ~stateregister_1_q_5, ~stateregister_1_q_6);  // AND_Gate
  and and_6 (and_6_out, X, stateregister_1_q_2, ~stateregister_1_q_4, ~stateregister_1_q_5, ~stateregister_1_q_6);  // AND_Gate
  and and_7 (and_7_out, X, stateregister_1_q_3, ~stateregister_1_q_4, ~stateregister_1_q_5, ~stateregister_1_q_6);  // AND_Gate
  and and_8 (and_8_out, stateregister_1_q_1, ~stateregister_1_q_2, ~stateregister_1_q_3, stateregister_1_q_4, ~stateregister_1_q_5, ~stateregister_1_q_6);  // AND_Gate
  and and_9 (and_9_out, E, ~stateregister_1_q_1, stateregister_1_q_2, ~stateregister_1_q_3, stateregister_1_q_5);  // AND_Gate
  and and_10 (and_10_out, ~E, ~stateregister_1_q_1, stateregister_1_q_2, stateregister_1_q_3, stateregister_1_q_6);  // AND_Gate
  and and_11 (and_11_out, X, stateregister_1_q_1, ~stateregister_1_q_4, ~stateregister_1_q_5, ~stateregister_1_q_6);  // AND_Gate
  and and_12 (and_12_out, ~stateregister_1_q_1, stateregister_1_q_2, ~stateregister_1_q_4, ~stateregister_1_q_5, ~stateregister_1_q_6);  // AND_Gate
  and and_13 (and_13_out, ~stateregister_1_q_1, stateregister_1_q_2, ~stateregister_1_q_3, ~stateregister_1_q_4);  // AND_Gate
  and and_14 (and_14_out, X, stateregister_1_q_2, ~stateregister_1_q_4, ~stateregister_1_q_5, ~stateregister_1_q_6);  // AND_Gate
  and and_15 (and_15_out, X, ~stateregister_1_q_2, stateregister_1_q_4, ~stateregister_1_q_5, ~stateregister_1_q_6);  // AND_Gate
  and and_16 (and_16_out, E, ~stateregister_1_q_1, stateregister_1_q_2, stateregister_1_q_3, stateregister_1_q_4);  // AND_Gate
  and and_17 (and_17_out, stateregister_1_q_1, ~stateregister_1_q_2, stateregister_1_q_6);  // AND_Gate
  and and_18 (and_18_out, ~X, E, stateregister_1_q_1, stateregister_1_q_2, ~stateregister_1_q_3);  // AND_Gate
  and and_19 (and_19_out, ~X, ~E, stateregister_1_q_3, ~stateregister_1_q_4, ~stateregister_1_q_5, ~stateregister_1_q_6);  // AND_Gate
  and and_20 (and_20_out, E, ~stateregister_1_q_1, stateregister_1_q_2, stateregister_1_q_3, ~stateregister_1_q_4, ~stateregister_1_q_6);  // AND_Gate
  and and_21 (and_21_out, X, stateregister_1_q_1, ~stateregister_1_q_4, ~stateregister_1_q_5, ~stateregister_1_q_6);  // AND_Gate
  and and_22 (and_22_out, E, ~stateregister_1_q_1, stateregister_1_q_2, ~stateregister_1_q_3, ~stateregister_1_q_4);  // AND_Gate
  and and_23 (and_23_out, X, ~stateregister_1_q_2, ~stateregister_1_q_3, stateregister_1_q_4, ~stateregister_1_q_5, ~stateregister_1_q_6);  // AND_Gate
  and and_24 (and_24_out, ~E, ~stateregister_1_q_1, stateregister_1_q_2, stateregister_1_q_3, stateregister_1_q_4);  // AND_Gate
  and and_25 (and_25_out, ~E, ~stateregister_1_q_1, stateregister_1_q_2, stateregister_1_q_3, stateregister_1_q_5);  // AND_Gate
  and and_26 (and_26_out, E, ~stateregister_1_q_1, stateregister_1_q_2, stateregister_1_q_4, stateregister_1_q_6);  // AND_Gate
  and and_27 (and_27_out, E, stateregister_1_q_1, ~stateregister_1_q_2);  // AND_Gate
  and and_28 (and_28_out, ~E, stateregister_1_q_2, ~stateregister_1_q_4, ~stateregister_1_q_5, ~stateregister_1_q_6);  // AND_Gate
  and and_29 (and_29_out, ~E, ~stateregister_1_q_1, stateregister_1_q_2, ~stateregister_1_q_4);  // AND_Gate
  and and_30 (and_30_out, X, stateregister_1_q_3, ~stateregister_1_q_4, ~stateregister_1_q_5, ~stateregister_1_q_6);  // AND_Gate
  and and_31 (and_31_out, stateregister_1_q_1, ~stateregister_1_q_2, stateregister_1_q_4);  // AND_Gate
  and and_32 (and_32_out, stateregister_1_q_1, ~stateregister_1_q_2, stateregister_1_q_5);  // AND_Gate
  and and_33 (and_33_out, X, ~stateregister_1_q_1, stateregister_1_q_2, ~stateregister_1_q_4, ~stateregister_1_q_5, ~stateregister_1_q_6);  // AND_Gate
  and and_34 (and_34_out, ~stateregister_1_q_1, stateregister_1_q_3, ~stateregister_1_q_4, ~stateregister_1_q_5, ~stateregister_1_q_6);  // AND_Gate
  and and_35 (and_35_out, ~X, ~stateregister_1_q_2, stateregister_1_q_3);  // AND_Gate
  and and_36 (and_36_out, X, ~stateregister_1_q_1, ~stateregister_1_q_2, ~stateregister_1_q_3, stateregister_1_q_4);  // AND_Gate
  and and_37 (and_37_out, stateregister_1_q_1, stateregister_1_q_2, ~stateregister_1_q_3, stateregister_1_q_4);  // AND_Gate
  and and_38 (and_38_out, stateregister_1_q_1, ~stateregister_1_q_2, stateregister_1_q_3, stateregister_1_q_4);  // AND_Gate
  and and_39 (and_39_out, X, ~stateregister_1_q_1, ~stateregister_1_q_2, ~stateregister_1_q_3, stateregister_1_q_5);  // AND_Gate
  and and_40 (and_40_out, stateregister_1_q_1, stateregister_1_q_2, ~stateregister_1_q_3, stateregister_1_q_5);  // AND_Gate
  and and_41 (and_41_out, stateregister_1_q_1, ~stateregister_1_q_2, stateregister_1_q_3, stateregister_1_q_5);  // AND_Gate
  and and_42 (and_42_out, ~stateregister_1_q_1, stateregister_1_q_2, stateregister_1_q_4, stateregister_1_q_5);  // AND_Gate
  and and_43 (and_43_out, X, ~stateregister_1_q_1, ~stateregister_1_q_3, ~stateregister_1_q_4, stateregister_1_q_6);  // AND_Gate
  and and_44 (and_44_out, stateregister_1_q_2, ~stateregister_1_q_3, ~stateregister_1_q_4, stateregister_1_q_6);  // AND_Gate
  and and_45 (and_45_out, ~E, ~stateregister_1_q_1, stateregister_1_q_2, ~stateregister_1_q_4, stateregister_1_q_6);  // AND_Gate
  and and_46 (and_46_out, ~X, ~E, ~stateregister_1_q_1, stateregister_1_q_3, stateregister_1_q_6);  // AND_Gate
  and and_47 (and_47_out, stateregister_1_q_1, ~stateregister_1_q_2, stateregister_1_q_3, stateregister_1_q_6);  // AND_Gate
  and and_48 (and_48_out, X, stateregister_1_q_1, ~stateregister_1_q_2, ~stateregister_1_q_5, ~stateregister_1_q_6);  // AND_Gate
  and and_49 (and_49_out, X, ~stateregister_1_q_1, stateregister_1_q_2, ~stateregister_1_q_4, ~stateregister_1_q_5, ~stateregister_1_q_6);  // AND_Gate
  and and_50 (and_50_out, ~X, E, stateregister_1_q_1, stateregister_1_q_2, stateregister_1_q_3, ~stateregister_1_q_4);  // AND_Gate
  and and_51 (and_51_out, ~X, ~stateregister_1_q_2, stateregister_1_q_4);  // AND_Gate
  and and_52 (and_52_out, stateregister_1_q_1, ~stateregister_1_q_3, stateregister_1_q_4);  // AND_Gate
  and and_53 (and_53_out, ~stateregister_1_q_2, stateregister_1_q_3, stateregister_1_q_4);  // AND_Gate
  and and_54 (and_54_out, X, ~stateregister_1_q_1, ~stateregister_1_q_2, ~stateregister_1_q_3, ~stateregister_1_q_4, stateregister_1_q_5);  // AND_Gate
  and and_55 (and_55_out, stateregister_1_q_1, stateregister_1_q_2, stateregister_1_q_3, ~stateregister_1_q_4, stateregister_1_q_5);  // AND_Gate
  and and_56 (and_56_out, X, ~stateregister_1_q_1, ~stateregister_1_q_2, ~stateregister_1_q_3, ~stateregister_1_q_4, stateregister_1_q_6);  // AND_Gate
  and and_57 (and_57_out, E, stateregister_1_q_2, stateregister_1_q_3, stateregister_1_q_6);
  and and_58 (and_58_out, stateregister_1_q_1, stateregister_1_q_2, stateregister_1_q_3, stateregister_1_q_6);
  and and_59 (and_59_out, stateregister_1_q_1, stateregister_1_q_4, stateregister_1_q_6);
  and and_60 (and_60_out, stateregister_1_q_2, stateregister_1_q_4, stateregister_1_q_6);
  and and_61 (and_61_out, X, stateregister_1_q_1, stateregister_1_q_2, ~stateregister_1_q_3, ~stateregister_1_q_4, ~stateregister_1_q_6);  // AND_Gate
  and and_62 (and_62_out, X, ~stateregister_1_q_1, stateregister_1_q_3, ~stateregister_1_q_4, ~stateregister_1_q_5, ~stateregister_1_q_6);  // AND_Gate
  and and_63 (and_63_out, X, ~stateregister_1_q_2, stateregister_1_q_3, ~stateregister_1_q_4, ~stateregister_1_q_6);  // AND_Gate
  and and_64 (and_64_out, stateregister_1_q_1, stateregister_1_q_2, stateregister_1_q_3, stateregister_1_q_4, ~stateregister_1_q_5);  // AND_Gate
  and and_65 (and_65_out, ~X, ~stateregister_1_q_2, stateregister_1_q_5);  // AND_Gate
  and and_66 (and_66_out, stateregister_1_q_1, ~stateregister_1_q_4, stateregister_1_q_5);  // AND_Gate
  and and_67 (and_67_out, stateregister_1_q_1, ~stateregister_1_q_3, stateregister_1_q_5);  // AND_Gate
  and and_68 (and_68_out, ~stateregister_1_q_2, stateregister_1_q_4, stateregister_1_q_5);  // AND_Gate
  and and_69 (and_69_out, X, ~stateregister_1_q_1, ~stateregister_1_q_2, ~stateregister_1_q_3, ~stateregister_1_q_4, stateregister_1_q_6);  // AND_Gate
  and and_70 (and_70_out, X, stateregister_1_q_1, stateregister_1_q_2, stateregister_1_q_3, ~stateregister_1_q_4, ~stateregister_1_q_5);  // AND_Gate
  and and_71 (and_71_out, X, ~stateregister_1_q_2, ~stateregister_1_q_3, stateregister_1_q_4, ~stateregister_1_q_5);  // AND_Gate
  and and_72 (and_72_out, stateregister_1_q_1, ~stateregister_1_q_2, ~stateregister_1_q_3, stateregister_1_q_4, ~stateregister_1_q_5);  // AND_Gate
  and and_73 (and_73_out, stateregister_1_q_1, stateregister_1_q_2, stateregister_1_q_3, stateregister_1_q_4, stateregister_1_q_5);
  and and_74 (and_74_out, ~X, ~stateregister_1_q_2, stateregister_1_q_6);  // AND_Gate
  and and_75 (and_75_out, stateregister_1_q_1, stateregister_1_q_6);
  and and_76 (and_76_out, stateregister_1_q_6, stateregister_1_q_3, ~stateregister_1_q_2);  // AND_Gate
  or or_1 (or_1_out, and_70_out, and_71_out, and_72_out, and_73_out, and_74_out, and_75_out, and_76_out);
  or or_2 (or_2_out, and_1_out, and_2_out, and_3_out, and_4_out, and_5_out, and_21_out, and_6_out, and_22_out, and_7_out, and_23_out, and_8_out, and_24_out, and_9_out, and_25_out, and_10_out, and_26_out);
  or or_3 (or_3_out, and_11_out, and_27_out, and_12_out, and_28_out, and_13_out, and_29_out, and_14_out, and_30_out, and_15_out, and_31_out, and_16_out, and_32_out, and_17_out);
  or or_4 (or_4_out, and_33_out, and_18_out, and_34_out, and_19_out, and_35_out, and_20_out, and_36_out, and_37_out, and_38_out, and_39_out, and_40_out, and_41_out, and_42_out, and_43_out, and_44_out, and_45_out, and_46_out, and_47_out);
  or or_5 (or_5_out, and_48_out, and_49_out, and_50_out, and_51_out, and_52_out, and_53_out, and_54_out, and_55_out, and_56_out, and_57_out, and_58_out, and_59_out, and_60_out);
  or or_6 (or_6_out, and_61_out, and_62_out, and_63_out, and_64_out, and_65_out, and_66_out, and_67_out, and_68_out, and_69_out);
  StateRegister stateregister_1 (
    .Q_1(stateregister_1_q_1), .Q_2(stateregister_1_q_2), .Q_3(stateregister_1_q_3),
    .Q_4(stateregister_1_q_4), .Q_5(stateregister_1_q_5), .Q_6(stateregister_1_q_6), .R(R), .D_2(or_3_out),
    .D_3(or_4_out), .D_4(or_5_out), .D_5(or_6_out), .D_6(or_1_out), .D_1(or_2_out), .CLK(CLK));
  and and_77 (and_77_out, ~stateregister_1_q_1, stateregister_1_q_2, ~stateregister_1_q_3, stateregister_1_q_4, ~stateregister_1_q_5, ~stateregister_1_q_6);  // AND_Gate
  and and_78 (and_78_out, ~stateregister_1_q_2, stateregister_1_q_3, stateregister_1_q_4);  // AND_Gate
  and and_79 (and_79_out, ~stateregister_1_q_2, stateregister_1_q_5);  // AND_Gate
  and and_80 (and_80_out, ~stateregister_1_q_2, stateregister_1_q_6);  // AND_Gate
  and and_81 (and_81_out, stateregister_1_q_1, stateregister_1_q_2, stateregister_1_q_4);
  and and_82 (and_82_out, stateregister_1_q_1, stateregister_1_q_2, stateregister_1_q_5);
  and and_83 (and_83_out, stateregister_1_q_1, stateregister_1_q_2, stateregister_1_q_6);
  and and_84 (and_84_out, ~stateregister_1_q_4, ~stateregister_1_q_5, ~stateregister_1_q_6);  // AND_Gate
  and and_85 (and_85_out, ~stateregister_1_q_2, ~stateregister_1_q_3, ~stateregister_1_q_5, ~stateregister_1_q_6);  // AND_Gate
  and and_86 (and_86_out, stateregister_1_q_1, ~stateregister_1_q_3, ~stateregister_1_q_5, ~stateregister_1_q_6);  // AND_Gate
  and and_87 (and_87_out, stateregister_1_q_1, stateregister_1_q_2);
  and and_88 (and_88_out, stateregister_1_q_2, stateregister_1_q_3);
  and and_89 (and_89_out, stateregister_1_q_2, stateregister_1_q_5);
  and and_90 (and_90_out, stateregister_1_q_2, stateregister_1_q_6);
  and and_91 (and_91_out, ~stateregister_1_q_1, stateregister_1_q_2, ~stateregister_1_q_3, stateregister_1_q_4, ~stateregister_1_q_5, ~stateregister_1_q_6);  // AND_Gate
  and and_92 (and_92_out, stateregister_1_q_1, ~stateregister_1_q_2, stateregister_1_q_3, stateregister_1_q_4);  // AND_Gate
  and and_93 (and_93_out, stateregister_1_q_1, ~stateregister_1_q_2, stateregister_1_q_5);  // AND_Gate
  and and_94 (and_94_out, stateregister_1_q_1, ~stateregister_1_q_2, stateregister_1_q_6);  // AND_Gate
  and and_95 (and_95_out, ~stateregister_1_q_5, stateregister_1_q_4, ~stateregister_1_q_3, ~stateregister_1_q_2);  // AND_Gate
  and and_96 (and_96_out, stateregister_1_q_6, stateregister_1_q_3, stateregister_1_q_2, stateregister_1_q_1);
  and and_97 (and_97_out, stateregister_1_q_6, stateregister_1_q_4);
  and and_98 (and_98_out, ~stateregister_1_q_6, ~stateregister_1_q_5, ~stateregister_1_q_4, stateregister_1_q_3);  // AND_Gate
  and and_99 (and_99_out, ~stateregister_1_q_6, ~stateregister_1_q_4, stateregister_1_q_3, stateregister_1_q_2, stateregister_1_q_1);  // AND_Gate
  and and_100 (and_100_out, stateregister_1_q_5, stateregister_1_q_4);
  and and_101 (and_101_out, stateregister_1_q_6, ~stateregister_1_q_4, ~stateregister_1_q_3);  // AND_Gate
  and and_102 (and_102_out, stateregister_1_q_6, ~stateregister_1_q_4, ~stateregister_1_q_1);  // AND_Gate
  and and_103 (and_103_out, stateregister_1_q_6, stateregister_1_q_3, ~stateregister_1_q_2, stateregister_1_q_1);  // AND_Gate
  and and_104 (and_104_out, ~stateregister_1_q_6, ~stateregister_1_q_5, ~stateregister_1_q_4, stateregister_1_q_2);  // AND_Gate
  and and_105 (and_105_out, ~stateregister_1_q_4, stateregister_1_q_2, ~stateregister_1_q_1);  // AND_Gate
  and and_106 (and_106_out, stateregister_1_q_4, stateregister_1_q_3, stateregister_1_q_2, stateregister_1_q_1);
  and and_107 (and_107_out, stateregister_1_q_5, ~stateregister_1_q_4, ~stateregister_1_q_3);  // AND_Gate
  and and_108 (and_108_out, stateregister_1_q_5, ~stateregister_1_q_4, ~stateregister_1_q_2);  // AND_Gate
  and and_109 (and_109_out, stateregister_1_q_5, ~stateregister_1_q_4, ~stateregister_1_q_1);  // AND_Gate
  and and_110 (and_110_out, stateregister_1_q_6, ~stateregister_1_q_4, ~stateregister_1_q_3);  // AND_Gate
  and and_111 (and_111_out, stateregister_1_q_6, ~stateregister_1_q_4, ~stateregister_1_q_2);  // AND_Gate
  and and_112 (and_112_out, stateregister_1_q_6, ~stateregister_1_q_4, ~stateregister_1_q_1);  // AND_Gate
  and and_113 (and_113_out, ~stateregister_1_q_6, ~stateregister_1_q_5, ~stateregister_1_q_4, stateregister_1_q_1);  // AND_Gate
  and and_114 (and_114_out, ~stateregister_1_q_6, ~stateregister_1_q_5, ~stateregister_1_q_2, stateregister_1_q_1);  // AND_Gate
  and and_115 (and_115_out, ~stateregister_1_q_3, stateregister_1_q_2, stateregister_1_q_1);  // AND_Gate
  and and_116 (and_116_out, stateregister_1_q_3, ~stateregister_1_q_2, stateregister_1_q_1);  // AND_Gate
  and and_117 (and_117_out, stateregister_1_q_5, stateregister_1_q_4, ~stateregister_1_q_1);  // AND_Gate
  and and_118 (and_118_out, stateregister_1_q_5, stateregister_1_q_3, ~stateregister_1_q_1);  // AND_Gate
  and and_119 (and_119_out, stateregister_1_q_6, stateregister_1_q_3, ~stateregister_1_q_1);  // AND_Gate
  or or_7 (C0, and_95_out, and_96_out, and_97_out);
  or or_8 (C_1, and_98_out, and_99_out, and_100_out, and_101_out, and_102_out, and_103_out);
  or or_9 (C_2, and_104_out, and_105_out, and_106_out, and_107_out, and_108_out, and_109_out, and_110_out, and_111_out, and_112_out);
  or or_10 (C_3, and_113_out, and_114_out, and_115_out, and_116_out, and_117_out, and_118_out, and_119_out);
  or or_11 (LE_1, and_77_out, and_78_out, and_79_out, and_80_out);
  or or_12 (LE_0, and_81_out, and_82_out, and_83_out);
  or or_13 (LX_1, and_84_out, and_85_out, and_86_out, and_87_out, and_88_out, and_89_out, and_90_out);
  or or_14 (LX_0, and_91_out, and_92_out, and_93_out, and_94_out);

  // Notes on the sheet:
  //   X
  //   X
  //   E
  //   E
  //   S5
  //   S0
  //   S0
  //   S5
endmodule

module TrafficLight (
  input  L_0,
  input  L_1,
  output Red,
  output Yellow,
  output Green
);

  wire not_1_out, not_2_out;

  not not_1 (not_1_out, L_0);
  not not_2 (not_2_out, L_1);
  and and_1 (Red, L_1, not_1_out);
  and and_2 (Yellow, not_2_out, L_0);
  and and_3 (Green, not_2_out, not_1_out);
endmodule

module FullAdder (
  input  C_1,
  input  A,
  input  B,
  output S,
  output C_0
);

  wire and_1_out, and_2_out, and_3_out, xor_1_out;

  xor xor_1 (xor_1_out, A, B);
  and and_1 (and_1_out, A, B);
  and and_2 (and_2_out, C_1, B);
  and and_3 (and_3_out, C_1, A);
  xor xor_2 (S, C_1, xor_1_out);
  or or_1 (C_0, and_1_out, and_2_out, and_3_out);
endmodule

module FourBitRippleCarryAdder (
  input  [3:0] A,
  input  [3:0] B,
  input  C_o,
  output C_i,
  output [3:0] S_0
);

  wire fulladder_2_c_0, fulladder_3_c_0, fulladder_4_c_0;

  FullAdder fulladder_1 (.C_0(C_o), .S(S_0[3]), .A(A[3]), .B(B[3]), .C_1(fulladder_2_c_0));
  FullAdder fulladder_2 (.C_0(fulladder_2_c_0), .S(S_0[2]), .A(A[2]), .B(B[2]), .C_1(fulladder_3_c_0));
  FullAdder fulladder_3 (.C_0(fulladder_3_c_0), .S(S_0[1]), .A(A[1]), .B(B[1]), .C_1(fulladder_4_c_0));
  FullAdder fulladder_4 (.C_0(fulladder_4_c_0), .S(S_0[0]), .A(A[0]), .B(B[0]), .C_1(C_i));
endmodule

module UpDownCounter (
  input  Down,
  input  CLK,
  input  Reset,
  output [3:0] Q
);

  wire fourbitripplecarryadder_1_c_i;
  wire [3:0] fourbitripplecarryadder_1_s_0, multiplexer_1_out;

  Multiplexer #(.width(4)) multiplexer_1 (.in0(4'b0001), .in1(4'b1111), .out(multiplexer_1_out), .sel(Down));
  Register #(.width(4)) register_1 (.D(fourbitripplecarryadder_1_s_0), .clk(CLK), .Q(Q), .clr(Reset));  // open: en
  FourBitRippleCarryAdder fourbitripplecarryadder_1 (
    .S_0(fourbitripplecarryadder_1_s_0), .C_i(fourbitripplecarryadder_1_c_i), .A(multiplexer_1_out), .B(Q));  // open: C_o
  // also tied to GND on the sheet: fourbitripplecarryadder_1_c_i
endmodule
